// Logisim project hw4.circ as structural Verilog: 12 circuits, main circuit main
module main (
  input  beq,
  input  j,
  input  jr,
  input  blt,
  input  jal,
  input  jal_2,
  input  \input ,
  input  Rwd,
  input  [2:0] shamt,
  input  RegWe,
  input  [2:0] ALUop,
  input  store,
  input  ALUinB,
  input  load,
  input  jal_3,
  input  reset,
  input  [2:0] rd,
  input  [2:0] rs,
  input  Rdst,
  input  [2:0] rt,
  input  [11:0] in_21,
  input  [5:0] immediate,
  input  input_2,
  input  \output 
);

  wire ALUinB_t, and_1_out, and_2_out, beq_t, blt_t, clk, in, j_t, jal_t, jr_t, load_t, lt, not_1_out,
       not_2_out, not_3_out, or_1_out, out, Rdst_t, RegWe_t, Rwd_t, store_t, valid, Zero;
  wire [2:0] ALUOp_t, destination, multiplexer_5_out;
  wire [6:0] keyboard_1_data;
  wire [11:0] addy;
  wire [15:0] alu_2_data_output, eximm, full_adder_1_result, multiplexer_1_out, multiplexer_2_out,
       multiplexer_3_out, multiplexer_6_out, multiplexer_7_out, multiplexer_8_out, multiplexer_9_out,
       multiplexer_10_out, multiplexer_11_out, n12_16_extend_1_out, n12_16_extend_2_out, PC___1, PC_output,
       ram_1_data, rsval, rtval, stroke;
  wire [15:12] ins;

  controlla controlla_1 (
    .OPCODE(ins), .RegWe(RegWe_t), .Rdst(Rdst_t), .ALUinB(ALUinB_t), .store(store_t), .load(load_t),
    .Rwd(Rwd_t), .beq(beq_t), .blt(blt_t), .j(j_t), .jr(jr_t), .jal(jal_t), .in(in), .out(out),
    .ALUOp(ALUOp_t));
  Register PC (.reset(reset), .Write_Enable(1'b1), .Input(multiplexer_11_out), .Output(PC_output), .clock(clk));
  ALU alu_1 (.ALU_Op(3'b000), .a(16'h1), .b(PC_output), .Data_Output(PC___1));  // open: Zero, shamt, le
  ROM #(.addrWidth(16), .dataWidth(16)) rom_1 (.addr(PC_output), .data({ins, addy}));  // open: sel
  // Probe on ins
  Multiplexer #(.width(16), .enable("false")) multiplexer_1 (
    .in0(16'h80), .in1(stroke), .out(multiplexer_1_out), .sel(valid));
  // Probe on multiplexer_3_out
  Multiplexer #(.width(16), .enable("false")) multiplexer_2 (
    .in0(multiplexer_8_out), .in1(PC___1), .out(multiplexer_2_out), .sel(jal_t));
  Multiplexer #(.width(16), .enable("false")) multiplexer_3 (
    .in0(multiplexer_2_out), .in1(multiplexer_1_out), .out(multiplexer_3_out), .sel(in));
  not not_1 (not_1_out, clk);
  Multiplexer #(.width(3), .enable("false")) multiplexer_4 (
    .in0(multiplexer_5_out), .in1(3'b111), .out(destination), .sel(jal_t));
  Multiplexer #(.width(3), .enable("false")) multiplexer_5 (
    .in0(addy[5:3]), .in1(addy[8:6]), .out(multiplexer_5_out), .sel(Rdst_t));
  RegisterFile registerfile_1 (
    .RegDestination(destination), .WriteData(multiplexer_3_out), .Reset(reset), .RegWE(RegWe_t),
    .RegSource1(addy[11:9]), .RegSource2(addy[8:6]), .clock(not_1_out), .RS1Val(rsval), .RS2Val(rtval));
  // Probe on rsval
  Keyboard keyboard_1 (.clk(clk), .re(in), .clr(reset), .avail(valid), .data(keyboard_1_data));
  Multiplexer #(.width(16), .enable("false")) multiplexer_6 (
    .in0(rtval), .in1(eximm), .out(multiplexer_6_out), .sel(ALUinB_t));
  _6_16_extend u_6_16_extend_1 (.in(addy[5:0]), .out(eximm));
  // Probe on addy[5:3]
  // Probe on addy[11:9]
  // Probe on addy[8:6]
  // Probe on multiplexer_6_out
  Clock clock_1 (.out(clk));
  _7_16_extend u_7_16_extend_1 (.in(keyboard_1_data), .out(stroke));
  ALU alu_2 (
    .ALU_Op(ALUOp_t), .a(rsval), .b(multiplexer_6_out), .Data_Output(alu_2_data_output), .Zero(Zero),
    .shamt(addy[2:0]), .le(lt));
  // Probe on addy[5:0]
  not not_2 (not_2_out, clk);
  TTY #(.rows(13), .cols(80)) tty_1 (.data(rsval[6:0]), .clk(not_2_out), .we(out), .clr(reset));
  // Probe on alu_2_data_output
  not not_3 (not_3_out, clk);
  Full_Adder full_adder_1 (.a(PC___1), .b(eximm), .sub(1'b0), .Result(full_adder_1_result));  // open: overflow
  and and_1 (and_1_out, beq_t, Zero);
  and and_2 (and_2_out, blt_t, lt);
  RAM #(.addrWidth(16), .dataWidth(16), .bus("separate")) ram_1 (
    .addr(alu_2_data_output), .din(rtval), .data(ram_1_data), .str(store_t), .clk(not_3_out), .ld(load_t));  // open: sel, clr
  Multiplexer #(.width(16), .enable("false")) multiplexer_7 (
    .in0(PC___1), .in1(full_adder_1_result), .out(multiplexer_7_out), .sel(or_1_out));
  or or_1 (or_1_out, and_1_out, and_2_out);
  // Probe on multiplexer_8_out
  Multiplexer #(.width(16), .enable("false")) multiplexer_8 (
    .in0(alu_2_data_output), .in1(ram_1_data), .out(multiplexer_8_out), .sel(Rwd_t));
  // Probe on ram_1_data
  // Probe on addy
  Multiplexer #(.width(16), .enable("false")) multiplexer_9 (
    .in0(multiplexer_7_out), .in1(n12_16_extend_1_out), .out(multiplexer_9_out), .sel(j_t));
  _12_16_extend u_12_16_extend_1 (.in(addy), .out(n12_16_extend_1_out));
  Multiplexer #(.width(16), .enable("false")) multiplexer_10 (
    .in0(multiplexer_9_out), .in1(rsval), .out(multiplexer_10_out), .sel(jr_t));
  Multiplexer #(.width(16), .enable("false")) multiplexer_11 (
    .in0(multiplexer_10_out), .in1(n12_16_extend_2_out), .out(multiplexer_11_out), .sel(jal_t));
  _12_16_extend u_12_16_extend_2 (.in(addy), .out(n12_16_extend_2_out));

  // Other names for the same wires on the sheet: imm[5:0] = addy[5:0]; ins[11:0] = addy; shamt_t[2:0] = addy[2:0];
  //   rd_t[2:0] = addy[5:3]; rt_t[2:0] = addy[8:6]; rs_t[2:0] = addy[11:9]; OPCODE[3:0] = ins

  // Notes on the sheet:
  //   contents of rom_1 (hex, n*v repeats v):
  //   6100 6903 2805 f008 62a0 e400 693f b002 203f
endmodule

module Register (
  input  clock,
  input  reset,
  input  Write_Enable,
  input  [15:0] Input,
  output [15:0] Output
);

  D_Flip_Flop d_ff_1 (.clk(clock), .D(Input[0]), .Q(Output[0]), .en(Write_Enable), .reset(reset));  // open: Qn, preset
  D_Flip_Flop d_ff_2 (.clk(clock), .D(Input[1]), .Q(Output[1]), .en(Write_Enable), .reset(reset));  // open: Qn, preset
  D_Flip_Flop d_ff_3 (.clk(clock), .D(Input[2]), .Q(Output[2]), .en(Write_Enable), .reset(reset));  // open: Qn, preset
  D_Flip_Flop d_ff_4 (.clk(clock), .D(Input[3]), .Q(Output[3]), .en(Write_Enable), .reset(reset));  // open: Qn, preset
  D_Flip_Flop d_ff_5 (.clk(clock), .D(Input[4]), .Q(Output[4]), .en(Write_Enable), .reset(reset));  // open: Qn, preset
  D_Flip_Flop d_ff_6 (.clk(clock), .D(Input[5]), .Q(Output[5]), .en(Write_Enable), .reset(reset));  // open: Qn, preset
  D_Flip_Flop d_ff_7 (.clk(clock), .D(Input[6]), .Q(Output[6]), .en(Write_Enable), .reset(reset));  // open: Qn, preset
  D_Flip_Flop d_ff_8 (.clk(clock), .D(Input[7]), .Q(Output[7]), .en(Write_Enable), .reset(reset));  // open: Qn, preset
  D_Flip_Flop d_ff_9 (.clk(clock), .D(Input[8]), .Q(Output[8]), .en(Write_Enable), .reset(reset));  // open: Qn, preset
  D_Flip_Flop d_ff_10 (.clk(clock), .D(Input[9]), .Q(Output[9]), .en(Write_Enable), .reset(reset));  // open: Qn, preset
  D_Flip_Flop d_ff_11 (
    .clk(clock), .D(Input[10]), .Q(Output[10]), .en(Write_Enable), .reset(reset));  // open: Qn, preset
  D_Flip_Flop d_ff_12 (
    .clk(clock), .D(Input[11]), .Q(Output[11]), .en(Write_Enable), .reset(reset));  // open: Qn, preset
  D_Flip_Flop d_ff_13 (
    .clk(clock), .D(Input[12]), .Q(Output[12]), .en(Write_Enable), .reset(reset));  // open: Qn, preset
  D_Flip_Flop d_ff_14 (
    .clk(clock), .D(Input[13]), .Q(Output[13]), .en(Write_Enable), .reset(reset));  // open: Qn, preset
  D_Flip_Flop d_ff_15 (
    .clk(clock), .D(Input[14]), .Q(Output[14]), .en(Write_Enable), .reset(reset));  // open: Qn, preset
  D_Flip_Flop d_ff_16 (
    .clk(clock), .D(Input[15]), .Q(Output[15]), .en(Write_Enable), .reset(reset));  // open: Qn, preset

  // Other names for the same wires on the sheet: clk = clock; _0 = Input[0]; _1 = Input[1]; _2 = Input[2];
  //   _3 = Input[3]; _4 = Input[4]; _5 = Input[5]; _6 = Input[6]; _7 = Input[7]; _8 = Input[8]; _9 = Input[9];
  //   _10 = Input[10]; _11 = Input[11]; _12 = Input[12]; _13 = Input[13]; _14 = Input[14]; _15 = Input[15];
  //   out0 = Output[0]; out1 = Output[1]; out2 = Output[2]; out3 = Output[3]; out4 = Output[4]; out5 = Output[5];
  //   out6 = Output[6]; out7 = Output[7]; out8 = Output[8]; out9 = Output[9]; out10 = Output[10]; out11 = Output[11];
  //   out12 = Output[12]; out13 = Output[13]; out14 = Output[14]; out15 = Output[15]; WE = Write_Enable
endmodule

module RegisterFile (
  input  [2:0] RegDestination,
  input  [15:0] WriteData,
  input  Reset,
  input  RegWE,
  input  [2:0] RegSource1,
  input  [2:0] RegSource2,
  input  clock,
  output [15:0] RS1Val,
  output [15:0] RS2Val
);

  wire and_1_out, and_2_out, and_3_out, and_4_out, and_5_out, and_6_out, and_7_out, reg1, reg2, reg3, reg4,
       reg5, reg6, reg7;
  wire [15:0] out0, out1, out2, out3, out4, out5, out6, out7;

  Decoder #(.select(3)) decoder_1 (
    .out1(reg1), .out2(reg2), .out3(reg3), .out4(reg4), .out5(reg5), .out6(reg6), .out7(reg7),
    .sel(RegDestination));  // open: out0, en
  Register Reg0 (.reset(Reset), .Write_Enable(1'b0), .Input(WriteData), .Output(out0), .clock(clock));
  Register u_Reg1 (.reset(Reset), .Write_Enable(and_1_out), .Input(WriteData), .Output(out1), .clock(clock));
  and and_1 (and_1_out, reg1, RegWE);
  // Probe on out1
  Register u_Reg2 (.reset(Reset), .Write_Enable(and_2_out), .Input(WriteData), .Output(out2), .clock(clock));
  and and_2 (and_2_out, reg2, RegWE);
  // Probe on out2
  Register u_Reg3 (.reset(Reset), .Write_Enable(and_3_out), .Input(WriteData), .Output(out3), .clock(clock));
  and and_3 (and_3_out, reg3, RegWE);
  // Probe on out3
  // Probe on out0
  and and_4 (and_4_out, reg4, RegWE);
  and and_5 (and_5_out, reg5, RegWE);
  Register u_Reg4 (.reset(Reset), .Write_Enable(and_4_out), .Input(WriteData), .Output(out4), .clock(clock));
  // Probe on out4
  Register u_Reg5 (.reset(Reset), .Write_Enable(and_5_out), .Input(WriteData), .Output(out5), .clock(clock));
  // Probe on out5
  Register u_Reg6 (.reset(Reset), .Write_Enable(and_6_out), .Input(WriteData), .Output(out6), .clock(clock));
  and and_6 (and_6_out, reg6, RegWE);
  // Probe on out6
  Register u_Reg7 (.reset(Reset), .Write_Enable(and_7_out), .Input(WriteData), .Output(out7), .clock(clock));
  and and_7 (and_7_out, reg7, RegWE);
  // Probe on out7
  Multiplexer #(.select(3), .width(16), .enable("false")) multiplexer_1 (
    .in0(out0), .in1(out1), .in2(out2), .in3(out3), .in4(out4), .in5(out5), .in6(out6), .in7(out7),
    .out(RS1Val), .sel(RegSource1));
  Multiplexer #(.select(3), .width(16), .enable("false")) multiplexer_2 (
    .in0(out0), .in1(out1), .in2(out2), .in3(out3), .in4(out4), .in5(out5), .in6(out6), .in7(out7),
    .out(RS2Val), .sel(RegSource2));

  // Other names for the same wires on the sheet: clk = clock; data[15:0] = WriteData; ReadR1[2:0] = RegSource1;
  //   ReadR2[2:0] = RegSource2; WE = RegWE

  // Notes on the sheet:
  //   RS2Val: pull=up
endmodule

module ALU (
  input  [2:0] ALU_Op,
  input  [15:0] a,
  input  [15:0] b,
  input  [2:0] shamt,
  output [15:0] Data_Output,
  output Zero,
  output le
);

  wire not_2_out, or_1_out;
  wire [15:0] add, LEF, \not , RIG, sub, \xor ;

  Full_Adder full_adder_1 (.a(a), .b(b), .sub(1'b0), .Result(add));  // open: overflow
  Full_Adder full_adder_2 (.a(a), .b(b), .sub(1'b1), .Result(sub));  // open: overflow
  assign \not  = ~a;  // NOT_Gate not_1, 16 bits wide
  assign \xor  = a ^ b;  // XOR_Gate xor_1, 16 bits wide
  not not_2 (not_2_out, Zero);
  left left_1 (.shamt(shamt), .in(a), .out(LEF));
  right right_1 (.shamt(shamt), .in(a), .out(RIG));
  or or_1 (or_1_out, sub[0], sub[1], sub[2], sub[3], sub[4], sub[5], sub[6], sub[7], sub[8], sub[9], sub[10], sub[11], sub[12], sub[13], sub[14], sub[15]);
  and and_1 (le, not_2_out, sub[15]);
  not not_3 (Zero, or_1_out);
  Multiplexer #(.select(3), .width(16), .enable("false")) multiplexer_1 (
    .in0(add), .in1(sub), .in2(\not ), .in3(\xor ), .in4(RIG), .in5(LEF), .out(Data_Output), .sel(ALU_Op));  // open: in6, in7

  // Other names for the same wires on the sheet: _0 = Zero; ALUop[2:0] = ALU_Op

  // Notes on the sheet:
  //   ALU_Op: pull=up
endmodule

module _1bit_add (
  input  cin,
  input  a,
  input  b,
  output sum,
  output cout
);

  wire and_1_out, and_2_out, xor_1_out;

  and and_1 (and_1_out, b, a);
  xor xor_1 (xor_1_out, a, b);
  or or_1 (cout, and_1_out, and_2_out);
  and and_2 (and_2_out, xor_1_out, cin);
  xor xor_2 (sum, cin, xor_1_out);
endmodule

// Adder
module Full_Adder (
  input  [15:0] a,
  input  [15:0] b,
  input  sub,
  output [15:0] Result,
  output overflow
);

  wire n1bit_add_1_cout, n1bit_add_2_cout, n1bit_add_3_cout, n1bit_add_4_cout, n1bit_add_5_cout,
       n1bit_add_6_cout, n1bit_add_7_cout, n1bit_add_8_cout, n1bit_add_9_cout, n1bit_add_10_cout,
       n1bit_add_11_cout, n1bit_add_12_cout, n1bit_add_13_cout, n1bit_add_14_cout, n1bit_add_15_cout,
       n1bit_add_16_cout, xor_1_out, xor_2_out, xor_3_out, xor_4_out, xor_5_out, xor_6_out, xor_7_out,
       xor_8_out, xor_9_out, xor_10_out, xor_11_out, xor_12_out, xor_13_out, xor_14_out, xor_15_out,
       xor_17_out;

  _1bit_add u_1bit_add_1 (.cin(sub), .a(a[0]), .b(xor_1_out), .sum(Result[0]), .cout(n1bit_add_1_cout));
  xor xor_1 (xor_1_out, sub, b[0]);
  _1bit_add u_1bit_add_2 (.cin(n1bit_add_1_cout), .a(a[1]), .b(xor_2_out), .sum(Result[1]), .cout(n1bit_add_2_cout));
  xor xor_2 (xor_2_out, sub, b[1]);
  _1bit_add u_1bit_add_3 (.cin(n1bit_add_2_cout), .a(a[2]), .b(xor_3_out), .sum(Result[2]), .cout(n1bit_add_3_cout));
  xor xor_3 (xor_3_out, sub, b[2]);
  _1bit_add u_1bit_add_4 (.cin(n1bit_add_3_cout), .a(a[3]), .b(xor_4_out), .sum(Result[3]), .cout(n1bit_add_4_cout));
  xor xor_4 (xor_4_out, sub, b[3]);
  _1bit_add u_1bit_add_5 (.cin(n1bit_add_4_cout), .a(a[4]), .b(xor_5_out), .sum(Result[4]), .cout(n1bit_add_5_cout));
  xor xor_5 (xor_5_out, sub, b[4]);
  _1bit_add u_1bit_add_6 (.cin(n1bit_add_5_cout), .a(a[5]), .b(xor_6_out), .sum(Result[5]), .cout(n1bit_add_6_cout));
  xor xor_6 (xor_6_out, sub, b[5]);
  _1bit_add u_1bit_add_7 (.cin(n1bit_add_6_cout), .a(a[6]), .b(xor_7_out), .sum(Result[6]), .cout(n1bit_add_7_cout));
  xor xor_7 (xor_7_out, sub, b[6]);
  _1bit_add u_1bit_add_8 (.cin(n1bit_add_7_cout), .a(a[7]), .b(xor_8_out), .sum(Result[7]), .cout(n1bit_add_8_cout));
  xor xor_8 (xor_8_out, sub, b[7]);
  _1bit_add u_1bit_add_9 (.cin(n1bit_add_8_cout), .a(a[8]), .b(xor_9_out), .sum(Result[8]), .cout(n1bit_add_9_cout));
  xor xor_9 (xor_9_out, sub, b[8]);
  _1bit_add u_1bit_add_10 (.cin(n1bit_add_9_cout), .a(a[9]), .b(xor_10_out), .sum(Result[9]), .cout(n1bit_add_10_cout));
  xor xor_10 (xor_10_out, sub, b[9]);
  _1bit_add u_1bit_add_11 (
    .cin(n1bit_add_10_cout), .a(a[10]), .b(xor_11_out), .sum(Result[10]), .cout(n1bit_add_11_cout));
  xor xor_11 (xor_11_out, sub, b[10]);
  _1bit_add u_1bit_add_12 (
    .cin(n1bit_add_11_cout), .a(a[11]), .b(xor_12_out), .sum(Result[11]), .cout(n1bit_add_12_cout));
  xor xor_12 (xor_12_out, sub, b[11]);
  _1bit_add u_1bit_add_13 (
    .cin(n1bit_add_12_cout), .a(a[12]), .b(xor_13_out), .sum(Result[12]), .cout(n1bit_add_13_cout));
  xor xor_13 (xor_13_out, sub, b[12]);
  _1bit_add u_1bit_add_14 (
    .cin(n1bit_add_13_cout), .a(a[13]), .b(xor_14_out), .sum(Result[13]), .cout(n1bit_add_14_cout));
  xor xor_14 (xor_14_out, sub, b[13]);
  _1bit_add u_1bit_add_15 (
    .cin(n1bit_add_14_cout), .a(a[14]), .b(xor_15_out), .sum(Result[14]), .cout(n1bit_add_15_cout));
  xor xor_15 (xor_15_out, sub, b[14]);
  xor xor_16 (overflow, n1bit_add_15_cout, n1bit_add_16_cout);
  _1bit_add u_1bit_add_16 (
    .cin(n1bit_add_15_cout), .a(a[15]), .b(xor_17_out), .sum(Result[15]), .cout(n1bit_add_16_cout));
  xor xor_17 (xor_17_out, sub, b[15]);

  // Other names for the same wires on the sheet: s0 = Result[0]; s1 = Result[1]; s2 = Result[2]; s3 = Result[3];
  //   s4 = Result[4]; s5 = Result[5]; s6 = Result[6]; s7 = Result[7]; s8 = Result[8]; s9 = Result[9];
  //   s10 = Result[10]; s11 = Result[11]; s12 = Result[12]; s13 = Result[13]; s14 = Result[14]; s15 = Result[15]
endmodule

// 6e
module _6_16_extend (
  input  [5:0] in,
  output [15:0] out
);


  assign out = {{11{in[5]}}, in[4:0]};
endmodule

// 12e
module _12_16_extend (
  input  [11:0] in,
  output [15:0] out
);


  assign out = {{5{in[11]}}, in[10:0]};
endmodule

// 7-16
module _7_16_extend (
  input  [6:0] in,
  output [15:0] out
);


  assign out = {{9{1'b0}}, in};
endmodule

module right (
  input  [2:0] shamt,
  input  [15:0] in,
  output [15:0] out
);

  wire multiplexer_1_out, multiplexer_2_out, multiplexer_3_out, multiplexer_4_out, multiplexer_5_out,
       multiplexer_6_out, multiplexer_7_out, multiplexer_8_out, multiplexer_9_out, multiplexer_10_out,
       multiplexer_11_out, multiplexer_12_out, multiplexer_13_out, multiplexer_16_out, multiplexer_17_out,
       multiplexer_18_out, multiplexer_19_out, multiplexer_20_out, multiplexer_24_out, multiplexer_25_out,
       multiplexer_26_out, multiplexer_27_out, multiplexer_28_out, multiplexer_31_out, multiplexer_32_out,
       multiplexer_33_out, multiplexer_34_out, multiplexer_35_out, multiplexer_39_out, multiplexer_40_out,
       multiplexer_41_out, multiplexer_45_out, xor_1_out;

  Multiplexer #(.enable("false")) multiplexer_1 (.in0(in[0]), .in1(in[1]), .out(multiplexer_1_out), .sel(shamt[0]));
  Multiplexer #(.enable("false")) multiplexer_2 (.in0(in[1]), .in1(in[2]), .out(multiplexer_2_out), .sel(shamt[0]));
  Multiplexer #(.enable("false")) multiplexer_3 (.in0(in[2]), .in1(in[3]), .out(multiplexer_3_out), .sel(shamt[0]));
  Multiplexer #(.enable("false")) multiplexer_4 (
    .in0(multiplexer_1_out), .in1(multiplexer_3_out), .out(multiplexer_4_out), .sel(shamt[1]));
  Multiplexer #(.enable("false")) multiplexer_5 (.in0(in[3]), .in1(in[4]), .out(multiplexer_5_out), .sel(shamt[0]));
  Multiplexer #(.enable("false")) multiplexer_6 (.in0(in[4]), .in1(in[5]), .out(multiplexer_6_out), .sel(shamt[0]));
  Multiplexer #(.enable("false")) multiplexer_7 (.in0(in[5]), .in1(in[6]), .out(multiplexer_7_out), .sel(shamt[0]));
  Multiplexer #(.enable("false")) multiplexer_8 (
    .in0(multiplexer_2_out), .in1(multiplexer_5_out), .out(multiplexer_8_out), .sel(shamt[1]));
  Multiplexer #(.enable("false")) multiplexer_9 (
    .in0(multiplexer_3_out), .in1(multiplexer_6_out), .out(multiplexer_9_out), .sel(shamt[1]));
  Multiplexer #(.enable("false")) multiplexer_10 (
    .in0(multiplexer_5_out), .in1(multiplexer_7_out), .out(multiplexer_10_out), .sel(shamt[1]));
  Multiplexer #(.enable("false")) multiplexer_11 (.in0(in[6]), .in1(in[7]), .out(multiplexer_11_out), .sel(shamt[0]));
  Multiplexer #(.enable("false")) multiplexer_12 (.in0(in[7]), .in1(in[8]), .out(multiplexer_12_out), .sel(shamt[0]));
  Multiplexer #(.enable("false")) multiplexer_13 (.in0(in[8]), .in1(in[9]), .out(multiplexer_13_out), .sel(shamt[0]));
  Multiplexer #(.enable("false")) multiplexer_14 (
    .in0(multiplexer_4_out), .in1(multiplexer_16_out), .out(out[0]), .sel(shamt[2]));
  Multiplexer #(.enable("false")) multiplexer_15 (
    .in0(multiplexer_8_out), .in1(multiplexer_17_out), .out(out[1]), .sel(shamt[2]));
  Multiplexer #(.enable("false")) multiplexer_16 (
    .in0(multiplexer_6_out), .in1(multiplexer_11_out), .out(multiplexer_16_out), .sel(shamt[1]));
  Multiplexer #(.enable("false")) multiplexer_17 (
    .in0(multiplexer_7_out), .in1(multiplexer_12_out), .out(multiplexer_17_out), .sel(shamt[1]));
  Multiplexer #(.enable("false")) multiplexer_18 (
    .in0(multiplexer_11_out), .in1(multiplexer_13_out), .out(multiplexer_18_out), .sel(shamt[1]));
  Multiplexer #(.enable("false")) multiplexer_19 (.in0(in[9]), .in1(in[10]), .out(multiplexer_19_out), .sel(shamt[0]));
  Multiplexer #(.enable("false")) multiplexer_20 (.in0(in[10]), .in1(in[11]), .out(multiplexer_20_out), .sel(shamt[0]));
  Multiplexer #(.enable("false")) multiplexer_21 (
    .in0(multiplexer_9_out), .in1(multiplexer_18_out), .out(out[2]), .sel(shamt[2]));
  Multiplexer #(.enable("false")) multiplexer_22 (
    .in0(multiplexer_10_out), .in1(multiplexer_24_out), .out(out[3]), .sel(shamt[2]));
  Multiplexer #(.enable("false")) multiplexer_23 (
    .in0(multiplexer_16_out), .in1(multiplexer_25_out), .out(out[4]), .sel(shamt[2]));
  Multiplexer #(.enable("false")) multiplexer_24 (
    .in0(multiplexer_12_out), .in1(multiplexer_19_out), .out(multiplexer_24_out), .sel(shamt[1]));
  Multiplexer #(.enable("false")) multiplexer_25 (
    .in0(multiplexer_13_out), .in1(multiplexer_20_out), .out(multiplexer_25_out), .sel(shamt[1]));
  Multiplexer #(.enable("false")) multiplexer_26 (.in0(in[11]), .in1(in[12]), .out(multiplexer_26_out), .sel(shamt[0]));
  Multiplexer #(.enable("false")) multiplexer_27 (.in0(in[12]), .in1(in[13]), .out(multiplexer_27_out), .sel(shamt[0]));
  Multiplexer #(.enable("false")) multiplexer_28 (.in0(in[13]), .in1(in[14]), .out(multiplexer_28_out), .sel(shamt[0]));
  xor xor_1 (xor_1_out, in[15], 1'b0);
  Multiplexer #(.enable("false")) multiplexer_29 (
    .in0(multiplexer_17_out), .in1(multiplexer_31_out), .out(out[5]), .sel(shamt[2]));
  Multiplexer #(.enable("false")) multiplexer_30 (
    .in0(multiplexer_18_out), .in1(multiplexer_32_out), .out(out[6]), .sel(shamt[2]));
  Multiplexer #(.enable("false")) multiplexer_31 (
    .in0(multiplexer_19_out), .in1(multiplexer_26_out), .out(multiplexer_31_out), .sel(shamt[1]));
  Multiplexer #(.enable("false")) multiplexer_32 (
    .in0(multiplexer_20_out), .in1(multiplexer_27_out), .out(multiplexer_32_out), .sel(shamt[1]));
  Multiplexer #(.enable("false")) multiplexer_33 (
    .in0(multiplexer_26_out), .in1(multiplexer_28_out), .out(multiplexer_33_out), .sel(shamt[1]));
  Multiplexer #(.enable("false")) multiplexer_34 (.in0(in[14]), .in1(in[15]), .out(multiplexer_34_out), .sel(shamt[0]));
  Multiplexer #(.enable("false")) multiplexer_35 (
    .in0(in[15]), .in1(xor_1_out), .out(multiplexer_35_out), .sel(shamt[0]));
  Multiplexer #(.enable("false")) multiplexer_36 (
    .in0(multiplexer_24_out), .in1(multiplexer_33_out), .out(out[7]), .sel(shamt[2]));
  Multiplexer #(.enable("false")) multiplexer_37 (
    .in0(multiplexer_25_out), .in1(multiplexer_39_out), .out(out[8]), .sel(shamt[2]));
  Multiplexer #(.enable("false")) multiplexer_38 (
    .in0(multiplexer_31_out), .in1(multiplexer_40_out), .out(out[9]), .sel(shamt[2]));
  Multiplexer #(.enable("false")) multiplexer_39 (
    .in0(multiplexer_27_out), .in1(multiplexer_34_out), .out(multiplexer_39_out), .sel(shamt[1]));
  Multiplexer #(.enable("false")) multiplexer_40 (
    .in0(multiplexer_28_out), .in1(multiplexer_35_out), .out(multiplexer_40_out), .sel(shamt[1]));
  Multiplexer #(.enable("false")) multiplexer_41 (
    .in0(multiplexer_34_out), .in1(xor_1_out), .out(multiplexer_41_out), .sel(shamt[1]));
  Multiplexer #(.enable("false")) multiplexer_42 (
    .in0(multiplexer_32_out), .in1(multiplexer_41_out), .out(out[10]), .sel(shamt[2]));
  Multiplexer #(.enable("false")) multiplexer_43 (
    .in0(multiplexer_33_out), .in1(multiplexer_45_out), .out(out[11]), .sel(shamt[2]));
  Multiplexer #(.enable("false")) multiplexer_44 (
    .in0(multiplexer_39_out), .in1(xor_1_out), .out(out[12]), .sel(shamt[2]));
  Multiplexer #(.enable("false")) multiplexer_45 (
    .in0(multiplexer_35_out), .in1(xor_1_out), .out(multiplexer_45_out), .sel(shamt[1]));
  Multiplexer #(.enable("false")) multiplexer_46 (
    .in0(multiplexer_40_out), .in1(xor_1_out), .out(out[13]), .sel(shamt[2]));
  Multiplexer #(.enable("false")) multiplexer_47 (
    .in0(multiplexer_41_out), .in1(xor_1_out), .out(out[14]), .sel(shamt[2]));
  Multiplexer #(.enable("false")) multiplexer_48 (
    .in0(multiplexer_45_out), .in1(xor_1_out), .out(out[15]), .sel(shamt[2]));

  // Other names for the same wires on the sheet: _15 = in[0]; _14 = in[1]; _13 = in[2]; _12 = in[3]; _11 = in[4];
  //   _10 = in[5]; _9 = in[6]; _8 = in[7]; _7 = in[8]; _6 = in[9]; _5 = in[10]; _4 = in[11]; _3 = in[12];
  //   _2b = in[13]; _1b = in[14]; _0b = in[15]; o15 = out[0]; o14 = out[1]; o13 = out[2]; o12 = out[3]; o11 = out[4];
  //   o10 = out[5]; o9 = out[6]; o8 = out[7]; o7 = out[8]; o6 = out[9]; o5 = out[10]; o4 = out[11]; o3 = out[12];
  //   o2 = out[13]; o1 = out[14]; o0 = out[15]; _0 = shamt[0]; _1 = shamt[1]; _2 = shamt[2]
endmodule

module left (
  input  [2:0] shamt,
  input  [15:0] in,
  output [15:0] out
);

  wire multiplexer_1_out, multiplexer_2_out, multiplexer_3_out, multiplexer_4_out, multiplexer_5_out,
       multiplexer_6_out, multiplexer_7_out, multiplexer_8_out, multiplexer_9_out, multiplexer_10_out,
       multiplexer_11_out, multiplexer_12_out, multiplexer_13_out, multiplexer_16_out, multiplexer_17_out,
       multiplexer_18_out, multiplexer_19_out, multiplexer_20_out, multiplexer_24_out, multiplexer_25_out,
       multiplexer_26_out, multiplexer_27_out, multiplexer_28_out, multiplexer_31_out, multiplexer_32_out,
       multiplexer_33_out, multiplexer_34_out, multiplexer_35_out, multiplexer_39_out, multiplexer_40_out,
       multiplexer_41_out, multiplexer_45_out;

  Multiplexer #(.enable("false")) multiplexer_1 (.in0(in[15]), .in1(in[14]), .out(multiplexer_1_out), .sel(shamt[0]));
  Multiplexer #(.enable("false")) multiplexer_2 (.in0(in[14]), .in1(in[13]), .out(multiplexer_2_out), .sel(shamt[0]));
  Multiplexer #(.enable("false")) multiplexer_3 (.in0(in[13]), .in1(in[12]), .out(multiplexer_3_out), .sel(shamt[0]));
  Multiplexer #(.enable("false")) multiplexer_4 (
    .in0(multiplexer_1_out), .in1(multiplexer_3_out), .out(multiplexer_4_out), .sel(shamt[1]));
  Multiplexer #(.enable("false")) multiplexer_5 (.in0(in[12]), .in1(in[11]), .out(multiplexer_5_out), .sel(shamt[0]));
  Multiplexer #(.enable("false")) multiplexer_6 (.in0(in[11]), .in1(in[10]), .out(multiplexer_6_out), .sel(shamt[0]));
  Multiplexer #(.enable("false")) multiplexer_7 (.in0(in[10]), .in1(in[9]), .out(multiplexer_7_out), .sel(shamt[0]));
  Multiplexer #(.enable("false")) multiplexer_8 (
    .in0(multiplexer_2_out), .in1(multiplexer_5_out), .out(multiplexer_8_out), .sel(shamt[1]));
  Multiplexer #(.enable("false")) multiplexer_9 (
    .in0(multiplexer_3_out), .in1(multiplexer_6_out), .out(multiplexer_9_out), .sel(shamt[1]));
  Multiplexer #(.enable("false")) multiplexer_10 (
    .in0(multiplexer_5_out), .in1(multiplexer_7_out), .out(multiplexer_10_out), .sel(shamt[1]));
  Multiplexer #(.enable("false")) multiplexer_11 (.in0(in[9]), .in1(in[8]), .out(multiplexer_11_out), .sel(shamt[0]));
  Multiplexer #(.enable("false")) multiplexer_12 (.in0(in[8]), .in1(in[7]), .out(multiplexer_12_out), .sel(shamt[0]));
  Multiplexer #(.enable("false")) multiplexer_13 (.in0(in[7]), .in1(in[6]), .out(multiplexer_13_out), .sel(shamt[0]));
  Multiplexer #(.enable("false")) multiplexer_14 (
    .in0(multiplexer_4_out), .in1(multiplexer_16_out), .out(out[15]), .sel(shamt[2]));
  Multiplexer #(.enable("false")) multiplexer_15 (
    .in0(multiplexer_8_out), .in1(multiplexer_17_out), .out(out[14]), .sel(shamt[2]));
  Multiplexer #(.enable("false")) multiplexer_16 (
    .in0(multiplexer_6_out), .in1(multiplexer_11_out), .out(multiplexer_16_out), .sel(shamt[1]));
  Multiplexer #(.enable("false")) multiplexer_17 (
    .in0(multiplexer_7_out), .in1(multiplexer_12_out), .out(multiplexer_17_out), .sel(shamt[1]));
  Multiplexer #(.enable("false")) multiplexer_18 (
    .in0(multiplexer_11_out), .in1(multiplexer_13_out), .out(multiplexer_18_out), .sel(shamt[1]));
  Multiplexer #(.enable("false")) multiplexer_19 (.in0(in[6]), .in1(in[5]), .out(multiplexer_19_out), .sel(shamt[0]));
  Multiplexer #(.enable("false")) multiplexer_20 (.in0(in[5]), .in1(in[4]), .out(multiplexer_20_out), .sel(shamt[0]));
  Multiplexer #(.enable("false")) multiplexer_21 (
    .in0(multiplexer_9_out), .in1(multiplexer_18_out), .out(out[13]), .sel(shamt[2]));
  Multiplexer #(.enable("false")) multiplexer_22 (
    .in0(multiplexer_10_out), .in1(multiplexer_24_out), .out(out[12]), .sel(shamt[2]));
  Multiplexer #(.enable("false")) multiplexer_23 (
    .in0(multiplexer_16_out), .in1(multiplexer_25_out), .out(out[11]), .sel(shamt[2]));
  Multiplexer #(.enable("false")) multiplexer_24 (
    .in0(multiplexer_12_out), .in1(multiplexer_19_out), .out(multiplexer_24_out), .sel(shamt[1]));
  Multiplexer #(.enable("false")) multiplexer_25 (
    .in0(multiplexer_13_out), .in1(multiplexer_20_out), .out(multiplexer_25_out), .sel(shamt[1]));
  Multiplexer #(.enable("false")) multiplexer_26 (.in0(in[4]), .in1(in[3]), .out(multiplexer_26_out), .sel(shamt[0]));
  Multiplexer #(.enable("false")) multiplexer_27 (.in0(in[3]), .in1(in[2]), .out(multiplexer_27_out), .sel(shamt[0]));
  Multiplexer #(.enable("false")) multiplexer_28 (.in0(in[2]), .in1(in[1]), .out(multiplexer_28_out), .sel(shamt[0]));
  Multiplexer #(.enable("false")) multiplexer_29 (
    .in0(multiplexer_17_out), .in1(multiplexer_31_out), .out(out[10]), .sel(shamt[2]));
  Multiplexer #(.enable("false")) multiplexer_30 (
    .in0(multiplexer_18_out), .in1(multiplexer_32_out), .out(out[9]), .sel(shamt[2]));
  Multiplexer #(.enable("false")) multiplexer_31 (
    .in0(multiplexer_19_out), .in1(multiplexer_26_out), .out(multiplexer_31_out), .sel(shamt[1]));
  Multiplexer #(.enable("false")) multiplexer_32 (
    .in0(multiplexer_20_out), .in1(multiplexer_27_out), .out(multiplexer_32_out), .sel(shamt[1]));
  Multiplexer #(.enable("false")) multiplexer_33 (
    .in0(multiplexer_26_out), .in1(multiplexer_28_out), .out(multiplexer_33_out), .sel(shamt[1]));
  Multiplexer #(.enable("false")) multiplexer_34 (.in0(in[1]), .in1(in[0]), .out(multiplexer_34_out), .sel(shamt[0]));
  Multiplexer #(.enable("false")) multiplexer_35 (.in0(in[0]), .in1(1'b0), .out(multiplexer_35_out), .sel(shamt[0]));
  Multiplexer #(.enable("false")) multiplexer_36 (
    .in0(multiplexer_24_out), .in1(multiplexer_33_out), .out(out[8]), .sel(shamt[2]));
  Multiplexer #(.enable("false")) multiplexer_37 (
    .in0(multiplexer_25_out), .in1(multiplexer_39_out), .out(out[7]), .sel(shamt[2]));
  Multiplexer #(.enable("false")) multiplexer_38 (
    .in0(multiplexer_31_out), .in1(multiplexer_40_out), .out(out[6]), .sel(shamt[2]));
  Multiplexer #(.enable("false")) multiplexer_39 (
    .in0(multiplexer_27_out), .in1(multiplexer_34_out), .out(multiplexer_39_out), .sel(shamt[1]));
  Multiplexer #(.enable("false")) multiplexer_40 (
    .in0(multiplexer_28_out), .in1(multiplexer_35_out), .out(multiplexer_40_out), .sel(shamt[1]));
  Multiplexer #(.enable("false")) multiplexer_41 (
    .in0(multiplexer_34_out), .in1(1'b0), .out(multiplexer_41_out), .sel(shamt[1]));
  Multiplexer #(.enable("false")) multiplexer_42 (
    .in0(multiplexer_32_out), .in1(multiplexer_41_out), .out(out[5]), .sel(shamt[2]));
  Multiplexer #(.enable("false")) multiplexer_43 (
    .in0(multiplexer_33_out), .in1(multiplexer_45_out), .out(out[4]), .sel(shamt[2]));
  Multiplexer #(.enable("false")) multiplexer_44 (.in0(multiplexer_39_out), .in1(1'b0), .out(out[3]), .sel(shamt[2]));
  Multiplexer #(.enable("false")) multiplexer_45 (
    .in0(multiplexer_35_out), .in1(1'b0), .out(multiplexer_45_out), .sel(shamt[1]));
  Multiplexer #(.enable("false")) multiplexer_46 (.in0(multiplexer_40_out), .in1(1'b0), .out(out[2]), .sel(shamt[2]));
  Multiplexer #(.enable("false")) multiplexer_47 (.in0(multiplexer_41_out), .in1(1'b0), .out(out[1]), .sel(shamt[2]));
  Multiplexer #(.enable("false")) multiplexer_48 (.in0(multiplexer_45_out), .in1(1'b0), .out(out[0]), .sel(shamt[2]));

  // Other names for the same wires on the sheet: _0b = in[0]; _1b = in[1]; _2b = in[2]; _3 = in[3]; _4 = in[4];
  //   _5 = in[5]; _6 = in[6]; _7 = in[7]; _8 = in[8]; _9 = in[9]; _10 = in[10]; _11 = in[11]; _12 = in[12];
  //   _13 = in[13]; _14 = in[14]; _15 = in[15]; o0 = out[0]; o1 = out[1]; o2 = out[2]; o3 = out[3]; o4 = out[4];
  //   o5 = out[5]; o6 = out[6]; o7 = out[7]; o8 = out[8]; o9 = out[9]; o10 = out[10]; o11 = out[11]; o12 = out[12];
  //   o13 = out[13]; o14 = out[14]; o15 = out[15]; _0 = shamt[0]; _1 = shamt[1]; _2 = shamt[2]
endmodule

module controlla (
  input  [3:0] OPCODE,
  output out,
  output in,
  output jal,
  output jr,
  output j,
  output [2:0] ALUOp,
  output beq,
  output blt,
  output store,
  output load,
  output Rwd,
  output Rdst,
  output ALUinB,
  output RegWe
);

  wire add, addi, \not , or_3_out, shl, shra, sub, \xor ;

  or or_1 (Rdst, load, addi);
  or or_2 (ALUinB, load, store, addi);
  Decoder #(.select(4), .enable("false")) decoder_1 (
    .out0(load), .out1(store), .out2(beq), .out3(blt), .out4(\not ), .out5(\xor ), .out6(addi), .out7(add),
    .out8(sub), .out9(shra), .out10(shl), .out11(j), .out12(jal), .out13(jr), .out14(out), .out15(in),
    .sel(OPCODE));
  or or_3 (or_3_out, \xor , \not , \not );
  or or_4 (RegWe, or_3_out, addi, add, load, shra, sub, jal, in, shl);
  or or_5 (ALUOp[0], \xor , sub, shl);
  or or_6 (ALUOp[1], \xor , \not );
  or or_7 (ALUOp[2], shra, shl);

  assign Rwd = load;

  // Other names for the same wires on the sheet: lw = load; sw = store

  // Notes on the sheet:
  //   OPCODE: pull=up
endmodule
